# Fritzing sketch Ultrasoon + Stepper + Podmeter + LCD (saved by Fritzing 0.9.4)
breadboards: 1

parts:
  Mod1 = Raspberry Pi 4B
  HC-SR04_Sensor_1 = HC-SR04 Ultrasonic Distance Sensor
  R1 = Resistor [tolerance=±5% resistance=1k package="0805 [SMD]"]
  R2 = Resistor [tolerance=±5% resistance=1k package="0805 [SMD]"]
  MOTOR1 = Adafruit Gear-Reduced Stepper Motor (small)
  BREAKOUT1 = ULN2003A breakout board
  IC1 = MCP3008 8-channel 10-bit ADC [part_number=MCP3008]
  U1 = POT [package=alps_pot]
  Nokia_5110_LCD_Module1 = Nokia 5110 LCD

nets:
  3V3: Mod1.3V3, IC1.no_name_yet#15, IC1.no_name_yet#16, U1.A, Nokia_5110_LCD_Module1.VCC, Nokia_5110_LCD_Module1.BL
  5V: Mod1.5V, HC-SR04_Sensor_1.VCC, R1.Pin_1, BREAKOUT1.+5V
  GND: Mod1.GND, HC-SR04_Sensor_1.GND, R2.Pin_0, BREAKOUT1.0V, IC1.no_name_yet#9, IC1.no_name_yet#14, U1.E, Nokia_5110_LCD_Module1.GND
  N1: Mod1.GPIO17, HC-SR04_Sensor_1.TRIG
  N2: Mod1.GPIO18, HC-SR04_Sensor_1.ECHO, R1.Pin_0, R2.Pin_1
  N3: Mod1.GPIO10, IC1.no_name_yet#11, Nokia_5110_LCD_Module1.Din
  N4: Mod1.GPIO9, IC1.no_name_yet#12
  N5: Mod1.GPIO11, IC1.no_name_yet#13, Nokia_5110_LCD_Module1.CLK
  N6: Mod1.GPIO8, IC1.no_name_yet#10
  N7: Mod1.GPIO7, Nokia_5110_LCD_Module1.CE
  N8: Mod1.GPIO5, Nokia_5110_LCD_Module1.D/C
  N9: Mod1.GPIO6, Nokia_5110_LCD_Module1.RST
  N10: MOTOR1.RED, BREAKOUT1.BLUE_wire
  N11: MOTOR1.ORANGE, BREAKOUT1.PINK_wire
  N12: MOTOR1.YELLOW, BREAKOUT1.YELLOW_wire
  N13: MOTOR1.PINK, BREAKOUT1.ORANGE_wire
  N14: MOTOR1.BLUE, BREAKOUT1.RED_wire
  N15: IC1.no_name_yet#1, U1.S

custom parts:
  Adafruit Gear-Reduced Stepper Motor (small): Adafruit gear-reduction stepper motor (small)
  ULN2003A breakout board: ULN2003A 7-way Darlington Transistor Driver on breakoutboard
  Nokia 5110 LCD: Nokia 5110 Graphic 84*48 LCD module <Blue Version>
