# Fritzing sketch Ultrasoon + Stepper (saved by Fritzing 0.9.4)
breadboards: 1

parts:
  Mod1 = Raspberry Pi 4B
  HC-SR04_Sensor_1 = HC-SR04 Ultrasonic Distance Sensor
  R1 = Resistor [tolerance=±5% resistance=1k package="0805 [SMD]"]
  R2 = Resistor [tolerance=±5% resistance=1k package="0805 [SMD]"]
  MOTOR1 = Adafruit Gear-Reduced Stepper Motor (small)
  IC1 = ULN2003A [package="SO16 [SMD]"]  # not connected
  BREAKOUT1 = ULN2003A breakout board

nets:
  5V: Mod1.5V, HC-SR04_Sensor_1.VCC, R1.Pin_1, BREAKOUT1.+5V
  GND: Mod1.GND, HC-SR04_Sensor_1.GND, R2.Pin_0, BREAKOUT1.0V
  N1: Mod1.GPIO17, HC-SR04_Sensor_1.TRIG
  N2: Mod1.GPIO18, HC-SR04_Sensor_1.ECHO, R1.Pin_0, R2.Pin_1
  N3: MOTOR1.RED, BREAKOUT1.BLUE_wire
  N4: MOTOR1.ORANGE, BREAKOUT1.PINK_wire
  N5: MOTOR1.YELLOW, BREAKOUT1.YELLOW_wire
  N6: MOTOR1.PINK, BREAKOUT1.ORANGE_wire
  N7: MOTOR1.BLUE, BREAKOUT1.RED_wire

custom parts:
  Adafruit Gear-Reduced Stepper Motor (small): Adafruit gear-reduction stepper motor (small)
  ULN2003A breakout board: ULN2003A 7-way Darlington Transistor Driver on breakoutboard
