# Fritzing sketch Ultrasoon (saved by Fritzing 0.9.4)
breadboards: 1

parts:
  Mod1 = Raspberry Pi 4B
  HC-SR04_Sensor_1 = HC-SR04 Ultrasonic Distance Sensor
  R1 = Resistor [tolerance=±5% resistance=1k package="0805 [SMD]"]
  R2 = Resistor [tolerance=±5% resistance=1k package="0805 [SMD]"]

nets:
  5V: Mod1.5V, HC-SR04_Sensor_1.VCC, R1.Pin_1
  GND: Mod1.GND, HC-SR04_Sensor_1.GND, R2.Pin_0
  N1: Mod1.GPIO17, HC-SR04_Sensor_1.TRIG
  N2: Mod1.GPIO18, HC-SR04_Sensor_1.ECHO, R1.Pin_0, R2.Pin_1
